// Logisim project CircuitProject.circ as structural Verilog: 1 circuit, main circuit main
module main (
  input  SW14,
  input  SW13,
  input  SW12,
  input  SW11,
  input  SW10,
  input  SW9,
  input  SW8,
  input  SW15,
  input  SW6,
  input  SW5,
  input  SW4,
  input  SW3,
  input  SW2,
  input  SW1,
  input  SW0,
  input  SW7
);

  wire comparator_1_gt, comparator_2_gt, comparator_3_gt, nor_1_out, or_1_out, or_2_out, or_3_out, or_4_out,
       or_5_out, or_6_out, or_7_out, or_8_out, or_9_out, or_10_out, register_1_q, shift_register_1_p1,
       shift_register_1_p2, shift_register_2_p1, shift_register_2_p2, shift_register_2_p21,
       shift_register_2_p22, shift_register_2_p23, shift_register_2_p24, shift_register_2_p25,
       shift_register_2_p26, shift_register_2_p27, undriven, undriven_2, undriven_3, xor_1_out;
  wire [3:0] adder_2_out, adder_3_out, adder_4_out, multiplexer_4_out, multiplexer_5_out, multiplexer_6_out,
       undriven_4;
  wire [6:0] multiplexer_1_out, multiplexer_2_out;
  wire [6:1] xor_2_out, xor_8_out;
  wire [13:0] adder_1_out, multiplexer_3_out, register_2_q, shift_register_1_p13;

  or or_1 (or_1_out, SW11, or_5_out);
  or or_2 (or_2_out, SW12, or_1_out);
  or or_3 (or_3_out, SW13, or_2_out);
  or or_4 (or_4_out, SW9, SW8);
  or or_5 (or_5_out, SW10, or_4_out);
  or or_6 (or_6_out, SW4, or_10_out);
  or or_7 (or_7_out, SW5, or_6_out);
  Register #(.width(1)) register_1 (.D(xor_1_out), .en(undriven), .Q(register_1_q));  // open: clk, clr
  xor xor_1 (xor_1_out, SW7, SW15);
  xor xor_2 (xor_2_out[1], SW8, SW9);
  xor xor_3 (xor_2_out[2], or_4_out, SW10);
  xor xor_4 (xor_2_out[3], or_5_out, SW11);
  xor xor_5 (xor_2_out[4], or_1_out, SW12);
  xor xor_6 (xor_2_out[5], or_2_out, SW13);
  xor xor_7 (xor_2_out[6], or_3_out, SW14);
  or or_8 (or_8_out, SW1, SW0);
  or or_9 (or_9_out, SW2, or_8_out);
  or or_10 (or_10_out, SW3, or_9_out);
  xor xor_8 (xor_8_out[1], SW0, SW1);
  xor xor_9 (xor_8_out[2], or_8_out, SW2);
  xor xor_10 (xor_8_out[3], or_9_out, SW3);
  xor xor_11 (xor_8_out[4], or_10_out, SW4);
  xor xor_12 (xor_8_out[5], or_6_out, SW5);
  xor xor_13 (xor_8_out[6], or_7_out, SW6);
  Multiplexer #(.width(7)) multiplexer_1 (
    .in0({SW14, SW13, SW12, SW11, SW10, SW9, SW8}), .in1({xor_2_out, SW8}), .out(multiplexer_1_out),
    .sel(SW15));
  Multiplexer #(.width(7)) multiplexer_2 (
    .in0({SW6, SW5, SW4, SW3, SW2, SW1, SW0}), .in1({xor_8_out, SW0}), .out(multiplexer_2_out), .sel(SW7));
  // Shift_Register #(.length(14)) shift_register_1: pin names not known; wires that end beside it: shift_register_1_p1, shift_register_1_p2, shift_register_1_p2, shift_register_1_p1, 1'b0, multiplexer_1_out[0], multiplexer_1_out[1], multiplexer_1_out[2], multiplexer_1_out[3], multiplexer_1_out[4], multiplexer_1_out[5], multiplexer_1_out[6], shift_register_1_p13[0], shift_register_1_p13[1], shift_register_1_p13[2], shift_register_1_p13[3], shift_register_1_p13[4], shift_register_1_p13[5]
  // Shift_Register #(.length(7)) shift_register_2: pin names not known; wires that end beside it: shift_register_2_p1, shift_register_2_p2, shift_register_2_p2, shift_register_2_p1, 1'b0, multiplexer_2_out[6], multiplexer_2_out[5], multiplexer_2_out[4], multiplexer_2_out[3], multiplexer_2_out[2], multiplexer_2_out[1], multiplexer_2_out[0], shift_register_1_p13[6], shift_register_1_p13[7], shift_register_1_p13[8], shift_register_1_p13[9], shift_register_1_p13[10], shift_register_1_p13[11], shift_register_1_p13[12], shift_register_1_p13[13], shift_register_2_p21, shift_register_2_p22, shift_register_2_p23, shift_register_2_p24, shift_register_2_p25, shift_register_2_p26, shift_register_2_p27
  nor nor_1 (nor_1_out, shift_register_2_p21, shift_register_2_p22, shift_register_2_p23, shift_register_2_p24, shift_register_2_p25, shift_register_2_p26, shift_register_2_p27);
  Adder #(.width(14)) adder_1 (
    .a(register_2_q), .b(shift_register_1_p13), .out(adder_1_out), .cin(1'b0));  // open: cout
  Register #(.width(14)) register_2 (.D(multiplexer_3_out), .en(undriven_3), .Q(register_2_q));  // open: clk, clr
  Multiplexer #(.width(14)) multiplexer_3 (
    .in0({14{1'b0}}), .in1(adder_1_out), .out(multiplexer_3_out), .sel(undriven_2));
  Adder #(.width(4)) adder_2 (.a(4'b0011), .b(4'b0000), .out(adder_2_out));  // open: cin, cout
  Comparator #(.mode("unsigned"), .width(4)) comparator_1 (
    .a(4'b0000), .b(4'b0100), .gt(comparator_1_gt));  // open: eq, lt
  Multiplexer #(.width(4)) multiplexer_4 (
    .in0(4'b0000), .in1(adder_2_out), .out(multiplexer_4_out), .sel(comparator_1_gt));
  Adder #(.width(4)) adder_3 (.a(4'b0011), .b({multiplexer_4_out[2:0], 1'b0}), .out(adder_3_out));  // open: cin, cout
  Comparator #(.mode("unsigned"), .width(4)) comparator_2 (
    .a({multiplexer_4_out[2:0], 1'b0}), .b(4'b0100), .gt(comparator_2_gt));  // open: eq, lt
  Adder #(.width(4)) adder_4 (.a(4'b0011), .b(undriven_4), .out(adder_4_out));  // open: cin, cout
  Comparator #(.mode("unsigned"), .width(4)) comparator_3 (
    .a(undriven_4), .b(4'b0100), .gt(comparator_3_gt));  // open: eq, lt
  Multiplexer #(.width(4)) multiplexer_5 (
    .in0({multiplexer_4_out[2:0], 1'b0}), .in1(adder_3_out), .out(multiplexer_5_out), .sel(comparator_2_gt));
  Multiplexer #(.width(4)) multiplexer_6 (
    .in0(undriven_4), .in1(adder_4_out), .out(multiplexer_6_out), .sel(comparator_3_gt));

  // Notes on the sheet:
  //   LI
  //   EShift
  //   EShift
  //   LI
  //   LI
  //   Psel
  //   Z
  //   B0
  //   Lp
  //   CU
endmodule
